// Logisim project 16by4ShiftReg.circ as structural Verilog: 1 circuit, main circuit 16by4ShiftReg
module _16by4ShiftReg (
  input  [3:0] Data,
  input  E,
  input  C,
  output [3:0] out_4,
  output [3:0] out_5,
  output [3:0] out_6,
  output [3:0] out_7,
  output [3:0] out_8,
  output [3:0] out_9,
  output [3:0] out_10,
  output [3:0] out_11,
  output [3:0] out_12,
  output [3:0] out_13,
  output [3:0] out_14,
  output [3:0] out_15,
  output [3:0] out_16,
  output [3:0] out_17,
  output [3:0] out_18,
  output [3:0] out_19
);

  Register #(.width(4)) register_1 (.D(out_4), .en(E), .Q(out_5), .clk(C));  // open: clr
  Register #(.width(4)) register_2 (.D(Data), .en(E), .Q(out_4), .clk(C));  // open: clr
  Register #(.width(4)) register_3 (.D(out_5), .en(E), .Q(out_6), .clk(C));  // open: clr
  Register #(.width(4)) register_4 (.D(out_6), .en(E), .Q(out_7), .clk(C));  // open: clr
  Register #(.width(4)) register_5 (.D(out_7), .en(E), .Q(out_8), .clk(C));  // open: clr
  Register #(.width(4)) register_6 (.D(out_8), .en(E), .Q(out_9), .clk(C));  // open: clr
  Register #(.width(4)) register_7 (.D(out_9), .en(E), .Q(out_10), .clk(C));  // open: clr
  Register #(.width(4)) register_8 (.D(out_10), .en(E), .Q(out_11), .clk(C));  // open: clr
  Register #(.width(4)) register_9 (.D(out_11), .en(E), .Q(out_12), .clk(C));  // open: clr
  Register #(.width(4)) register_10 (.D(out_12), .en(E), .Q(out_13), .clk(C));  // open: clr
  Register #(.width(4)) register_11 (.D(out_13), .en(E), .Q(out_14), .clk(C));  // open: clr
  Register #(.width(4)) register_12 (.D(out_15), .en(E), .Q(out_16), .clk(C));  // open: clr
  Register #(.width(4)) register_13 (.D(out_14), .en(E), .Q(out_15), .clk(C));  // open: clr
  Register #(.width(4)) register_14 (.D(out_16), .en(E), .Q(out_17), .clk(C));  // open: clr
  Register #(.width(4)) register_15 (.D(out_17), .en(E), .Q(out_18), .clk(C));  // open: clr
  Register #(.width(4)) register_16 (.D(out_18), .en(E), .Q(out_19), .clk(C));  // open: clr
endmodule
