// Logisim project UnyCount.circ as structural Verilog: 1 circuit, main circuit UnyCout
module UnyCout (
  input  [3:0] Step,
  input  Dir,
  input  [3:0] Max,
  input  Cin,
  input  wr,
  input  [3:0] Start,
  output [3:0] Value
);

  wire and_1_out, and_2_out, and_3_out, comparator_1_eq, comparator_1_gt, comparator_1_lt, not_3_out,
       not_4_out, or_1_out, or_2_out;
  wire [1:0] _1;
  wire [5:0] _2, _3, _4, adder_1_out, adder_3_out, multiplexer_1_out, multiplexer_2_out, multiplexer_3_out,
       not_1_out, not_2_out;
  wire [5:4] register_1_q;

  or or_1 (or_1_out, Cin, wr);
  assign not_1_out = ~{2'b00, Step};  // NOT_Gate not_1, 6 bits wide
  assign not_2_out = ~{2'b00, Max};  // NOT_Gate not_2, 6 bits wide
  Adder #(.width(6)) adder_1 (.a(not_1_out), .b(6'b000001), .out(adder_1_out));  // open: cin, cout
  Multiplexer #(.select(2), .width(6), .disabled(0), .enable("false")) multiplexer_1 (
    .in0(_3), .in1(_2), .in2(_4), .out(multiplexer_1_out), .sel(_1));  // open: in3
  Multiplexer #(.width(6), .disabled(0), .enable("false")) multiplexer_2 (
    .in0(multiplexer_1_out), .in1({2'b00, Start}), .out(multiplexer_2_out), .sel(wr));
  Multiplexer #(.width(6), .disabled(0), .enable("false")) multiplexer_3 (
    .in0({2'b00, Step}), .in1(adder_1_out), .out(multiplexer_3_out), .sel(Dir));
  Register #(.width(6), .trigger("falling")) register_1 (
    .D(multiplexer_2_out), .en(1'b1), .Q({register_1_q, Value}), .clk(or_1_out));  // open: clr
  Adder #(.width(6)) adder_2 (.a(_2), .b(not_2_out), .out(_3));  // open: cin, cout
  Adder #(.width(6)) adder_3 (.a(_2), .b(6'b000001), .out(adder_3_out));  // open: cin, cout
  Adder #(.width(6)) adder_4 (.a(adder_3_out), .b({2'b00, Max}), .out(_4));  // open: cin, cout
  Adder #(.width(6)) adder_5 (.a(multiplexer_3_out), .b({register_1_q, Value}), .out(_2));  // open: cin, cout
  not not_3 (not_3_out, _2[5]);
  not not_4 (not_4_out, _2[5]);
  Comparator #(.width(6)) comparator_1 (
    .a(_2), .b({2'b00, Max}), .gt(comparator_1_gt), .eq(comparator_1_eq), .lt(comparator_1_lt));
  or or_2 (or_2_out, comparator_1_eq, comparator_1_lt);
  and and_1 (and_1_out, not_4_out, comparator_1_gt);
  and and_2 (and_2_out, or_2_out, not_3_out);
  and and_3 (and_3_out, comparator_1_lt, _2[5]);
  Priority_Encoder #(.select(2), .disabled(0)) priority_encoder_1 (
    .in0(and_1_out), .in1(and_2_out), .in2(and_3_out), .out(_1));  // open: in3, gs, en_out, en_in

  // Other names for the same wires on the sheet: _5[3:0] = Start

  // Notes on the sheet:
  //   0 - сложение
  //   Шаг в дополнительном коде
  //   Прогнозируемое значение
  //   В регистр записывается разница прогноза и максимума за вычетом 1, необходимой для обнуления
  //   используется дополнительный код. +1, возникающая при переводе макс. в доп код и -1 для обнуления взаимно уничтожаются
  //   Прогноз > макс и знак +
  //   Прогноз <= макс и знак +
  //   Прогноз < макс и знак -
endmodule
