// Logisim project proverka21.circ as structural Verilog: 1 circuit, main circuit proverkaChip21
module proverkaChip21 (
  input  C,
  input  in_2,
  input  [11:0] in_3,
  output [3:0] out_4,
  output out_5,
  output [15:0] out_6,
  output [15:0] out_7
);

  wire and_1_out, and_2_out, counter_1_carry, d_ff_1_q, d_ff_1_qn, not_1_out;
  wire [15:0] controlled_buffer_1_out, shift_register_1_q0;

  Counter #(.width(4), .max('hf), .ongoal("stay")) counter_1 (
    .count(C), .Q(out_4), .carry(counter_1_carry), .clk(C));  // open: load, D, clr
  not not_1 (not_1_out, C);
  and and_1 (and_1_out, counter_1_carry, not_1_out);
  D_Flip_Flop d_ff_1 (.clk(C), .D(and_1_out), .Q(d_ff_1_q), .Qn(d_ff_1_qn));  // open: preset, en, reset
  and and_2 (and_2_out, d_ff_1_qn, C);
  ROM #(.addrWidth(12), .dataWidth(16)) rom_1 (.addr(in_3), .data(out_6));  // open: sel
  Shift_Register #(.length(16)) shift_register_1 (
    .shift(1'b1), .in(in_2), .clk(and_2_out), .q0(shift_register_1_q0[0]), .q1(shift_register_1_q0[1]),
    .q2(shift_register_1_q0[2]), .q3(shift_register_1_q0[3]), .q4(shift_register_1_q0[4]),
    .q5(shift_register_1_q0[5]), .q6(shift_register_1_q0[6]), .q7(shift_register_1_q0[7]),
    .q8(shift_register_1_q0[8]), .q9(shift_register_1_q0[9]), .q10(shift_register_1_q0[10]),
    .q11(shift_register_1_q0[11]), .q12(shift_register_1_q0[12]), .q13(shift_register_1_q0[13]),
    .q14(shift_register_1_q0[14]), .q15(shift_register_1_q0[15]));  // open: out, load, clr, d0, d1, d2, d3, d4, d5, d6, d7, d8, d9, d10, d11, d12, d13, d14, d15
  assign controlled_buffer_1_out = d_ff_1_q ? out_6 : 16'bz;  // Controlled_Buffer controlled_buffer_1
  Comparator #(.width(16)) comparator_1 (
    .a(controlled_buffer_1_out), .b(shift_register_1_q0), .eq(out_5));  // open: gt, lt
  assign out_7 = shift_register_1_q0 ^ controlled_buffer_1_out;  // XOR_Gate xor_1, 16 bits wide

  // Notes on the sheet:
  //   Вход логической функции
  //    (Номер варианта - 1) как двоичное 10ти разрядное число
  //   contents of rom_1 (hex, n*v repeats v):
  //   eaf2 ebf f3aa bf34 b6ba bf85 d49f 74bd 9fc5 7f2c ed39 ee6a 3aeb fb07 ae57 8eee fe54 b6ad 3d3b f16e
  //   3cf5 f798 f669 ae3e 7b8d f6b1 cdcb ecba c9bb ab67 bc9d b63e cf17 79ce 57da 9fa9 3be6 6ced 79ae d95d
  //   d72e d7b1 b1be c7f4 713f cf95 98ef 2d9f ef86 c5fc de3c d4db e93b f3d1 af65 de3a 8fe3 d78d 49fb b19f
  //   fba4 bb0f e1af ba4f e98f d35b d1f5 5abb 65f6 5d2f fa17 6b9e 4f97 de2d dd56 f78a 7573 7cba f8f1 175f
  //   eaae ebb2 9cf5 d799 7ba6 68fb efa1 55b7 cdcd 7676 bcf4 69dd abba dd53 3eea bfd 656f da7a 798f eda3
  //   9dc7 79d3 bef e5d6 59de e397 f359 bce9 cd73 a5eb daf2 4bf5 f9b1 deca e3d6 8fd6 776c b32f 75a7 ad6d
  //   e7a5 d71d 5de9 e86f ab3e d75c d8db 137f d36e 7f0b 3e9d c99f df89 ed17 d3f2 b1cf c7e6 d55b f5f0 4ebe
  //   3797 71db f179 74af dc7c 7b2b 993f 5dce 7ee1 acf6 f78c ce7a 70ef ab9d cbe6 72af be2e b45f 9f66 555f
  //   353f 6e3b 79da 6db6 8fa7 b56d bf15 9d3b 15bf df31 cfe4 cb76 9df4 e9bc 7e93 8fdc f707 7dd4 d61f 1bbb
  //   6a7b cdab b2be f38e 59e7 74f5 d85f eaba bd6c c93f 5add ef85 397d aef2 795e f2f4 39fa b9ce 9f93 4baf
  //   73ad 37d9 77b2 6dbc cfc3 b63d 97e5 71bb cabe 73ea 7477 6dd9 2bf6 dd72 8f9b 38fe 70fd dd5c b727 fc71
  //   335f d8be dd4d dde1 f6c6 ff03 13fe 5eb5 3d8f 5b8f d27b fb2c 73cb eb8b 16ef e63b 751f eabc d7d2 6ade
  //   d38f 5757 4f9b d99e 3e97 acbd e94f 8bf6 93eb ba3e 5d5d bb72 4efa 1dbd c6fa 1f6d fc55 fcaa 375b e9e6
  //   5bbc d63b 78fc b8f9 cbd5 ea37 c377 dec3 a97e dcdc 47f3 3fc3 c75d b375 d957 799b 77a6 f1e3 6c3f 2beb
  //   a3bb ccf3 d2ee b667 bf4c f8ea 1ed7 77d4 71de 8cef 57ea af8b d7e8 9fd8 f63a 3eec ede4 de5c da76 e9b3
  //   a5b7 fe83 da9b edc5 57e9 61df 3f99 79e5 a1df 3c7d 38fb ae5d 5fcc 9b97 17af d69b caf6 dc4f cdea da4f
  //   d2fa b3e3 a5db 26fb 76e5 f3ac a3f9 67c7 76e3 be69 3fd4 6d7c a56f b5d9 bf0e ef89 4fea ed1e 8ee7 feb0
  //   e3dc d979 fb45 6cd7 78eb 6dce 87fc 71b7 9ee5 def b5ad dccb e6f8 fda1 dfd f0bb da8f 8f75 ebe1 faca
  //   35de ff05 72ee ea76 eb96 27ee 99db 3d6d d5cb 87af f89b a3d7 afa5 ea4f bf1a 7277 f655 3db9 fab8 3ee9
  //   6bd3 ccaf ece9 d8dd d43f f965 b26f 27f5 d4bb eeb2 47cf 2dde a977 bbf0 ba1f d72d cf65 5dd9 e4ee 1eeb
  //   9e7c 679e 2df5 2ff2 6ce7 c5bb 2f57 9f8e f83d 6ead 4b6f 5caf be71 57a7 78d7 da67 a75d 927f 4ecf 6f0f
  //   bd87 d177 b6b6 bef0 f6a3 f5d2 da79 db5a 4de7 695f be96 fc56 a2df e3ba b5f2 f6cc d6ad cf2b 6e8f 766d
  //   3e8f faac 8dd7 f879 95d7 e8d7 ae97 6bae b91f cf66 e72b bdf 7bc9 9775 adb6 cf71 fb0d 63af 671f bd2e
  //   f26d fa8e 67e5 fa69 e78d 877e b74e b58f 75e3 6af5 d967 f36c bbca 56bb 9f53 eba3 bc6e 4bf9 f9e4 f663
  //   a7ec d6e6 fca5 c3bb fe2c 26f7 be65 fd4c ef43 5fd4 7f38 35af b6f2 dacd ecf1 c2fb 2dcf a99f e5d5 ef70
  //   6bad dde4 f395 8ed7 5be6 c7cb ce5e f077 b373 dec5 dd36 70fb 71fa 53cf 55fc ccfc 43fe 6f2b 1e7b a6f5
  //   7ce5 1deb ed4e 9e6b 2b7e 54fd ce3e fb29 5cbe f6ac 6b5e b95b b3da c1fb ef64 3adb 7f68 1efa 7e4b 793b
  //   6df2 d6da deb1 cd76 ff28 d573 93f5 13fb b2dd 96bb 9dad 8b9f fad2 b7e4 cf8d 8f7a 7de4 676e f74c 7ed1
  //   ccdd dd2e e4f5 b2fa a71f 6e5b 9dd3 6a77 7ae3 7b72 be1d 3c7e f2e5 d557 a8f7 f92d bbd8 fa87 765d bbd2
  //   ef83 9b75 e4be 9fc6 39fc 65be f23d bd9c e2fc fcb1 7ad3 b86f 776a 2d5f 7eb4 b2ee fb26 7dd8 11ff f56a
  //   c8f7 7b9a 68f7 dcd9 d6e9 f1ec 73da bb63 957d 35ee bfa4 7bf0 b597 87f5 3be5 c9e7 7c75 65bb cd1f 8e77
  //   a9eb 69e7 ccdb b5f4 e53b 9e73 55dd 7cd5 5e73 94f7 e9e3 5977 ff11 ecd6 f794 b9b3 7eca 74db cbcd a6ee
  //   e5e9 56db cfd4 d9e9 fc59 df4c 5db5 f596 6bf2 abea 9abe f764 53be e31f 5e9d 8afd af87 6f4b 65af fed0
  //   4fe5 fae2 cd5b 92fb 5b6d f749 6e7a cea7 e9b5 36f5 ce75 d9ec 4dee fe1c 7b65 d99d d6d3 f2b6 bea3 bdb8
  //   4fd5 975d 3cbd ef31 e9e9 5f1e 2af7 47f5 b59e 3ff0 f716 37ce 66be e4e7 db2b bd39 765e dab3 bec5 5b5e
  //   be2b 6c6f 66eb b3d9 bf68 df38 fd58 af9a 5cfa b6cb e2ee df43 dd8b 95dd fc65 f6b8 6e75 2d77 b755 e1bd
  //   e2db f4ea d676 c5ed e877 2f3e da9e 55bd 63fa a9db f9c6 e0f7 f574 753e e5ad 971f f54d 5fa5 fcb2 9dcb
  //   af17 75d9 bec6 b976 ed35 f987 9b5e d733 4fba c737 cb5e f2c7 f8ad eab6 f1ea eb1d 355f 3779 6f2d ebe2
  //   6e9e 32fb e3e6 57b3 59bb abe5 de27 df8a 567d 7b56 f4e5 87ed a6de f85b be3a 8777 db5c f13d cd6d 8fb6
  //   cfac d997 cfd2 cef1 eba6 eeb1 3e5d abf1 eae5 bee2 cadd 7c7a 5d73 69cf f7e d4f9 eb8e 45df 697b a9f5
  //   3fac b7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
  //   Входной набор для функции со счетчика
  //   Результат оценки 1 - правильно
  //   Диагностика ошибок
endmodule
