// Logisim project 10.circ as structural Verilog: 1 circuit, main circuit main
module main (
  input  not_S,
  input  R,
  input  not_R,
  input  S,
  input  not_S_2,
  input  S_2,
  input  S_3,
  input  C,
  input  \С ,
  input  R_2,
  input  R_3,
  input  not_R_2,
  input  D,
  input  D_2,
  input  C_2,
  input  C_3,
  input  not_S_3,
  input  not_S_4,
  input  not_R_3,
  input  not_R_4,
  input  T,
  input  C_4,
  input  not_S_5,
  input  not_S_6,
  input  T_2,
  input  not_R_5,
  input  not_R_6,
  input  not_S_7,
  input  \С_2 ,
  input  not_R_7,
  input  not_S_8,
  input  J,
  input  C_5,
  input  K,
  input  not_R_8,
  input  not_S_9,
  input  J_2,
  input  C_6,
  input  K_2,
  input  not_R_9
);

  wire clock_1_out, clock_2_out, clock_3_out, nand_2_out, nand_3_out, nand_4_out, nand_5_out, nand_6_out,
       nand_7_out, nand_8_out, nand_9_out, nand_10_out, nand_11_out, nand_12_out, nand_13_out, nand_14_out,
       nand_15_out, nand_16_out, nand_17_out, nand_18_out, nand_19_out, nand_20_out, nand_21_out,
       nand_22_out, nand_23_out, nand_24_out, nand_25_out, nand_26_out, nand_27_out, nand_28_out,
       nand_29_out, nand_30_out, nand_31_out, nand_32_out, nand_33_out, nand_34_out, nand_35_out,
       nand_36_out, nand_37_out, nand_38_out, nand_39_out, nand_40_out, nand_41_out, nand_42_out,
       nand_43_out, nand_44_out, nand_45_out, nand_46_out, nand_47_out, nand_48_out, nand_49_out,
       nand_50_out, nand_51_out, nand_52_out, nand_53_out, nand_54_out, nand_55_out, nand_56_out,
       nand_57_out, nand_58_out, nand_59_out, nand_60_out, nand_61_out, nand_62_out, nand_63_out,
       nand_64_out, nand_65_out, nand_66_out, nand_67_out, nand_68_out, nand_69_out, nand_70_out,
       nand_71_out, nand_72_out, nand_73_out, nor_1_out, nor_2_out, nor_3_out, nor_4_out, nor_5_out,
       nor_6_out, nor_7_out, nor_8_out;

  Clock clock_1 (.out(clock_1_out));
  // NAND_Gate nand_1 has open pins: in0=T, in1=C_4, out=open
  nand nand_2 (nand_2_out, not_S, nand_3_out);
  nand nand_3 (nand_3_out, nand_2_out, not_R);
  nand nand_4 (nand_4_out, S_2, C);
  nand nand_5 (nand_5_out, nand_4_out, nand_6_out);
  nand nand_6 (nand_6_out, nand_5_out, nand_7_out);
  nand nand_7 (nand_7_out, C, R_2);
  nand nand_8 (nand_8_out, D, C_2);
  nand nand_9 (nand_9_out, C_2, nand_10_out);
  nand nand_10 (nand_10_out, D, D);
  nand nand_11 (nand_11_out, nand_16_out, not_S_3);
  nand nand_12 (nand_12_out, not_R_3, nand_17_out);
  nand nand_13 (nand_13_out, T_2, T_2);
  LED led_1 (.in(nand_2_out));
  LED led_2 (.in(nand_3_out));
  LED led_3 (.in(nand_5_out));
  LED led_4 (.in(nand_6_out));
  nand nand_14 (nand_14_out, nand_8_out, nand_15_out);
  nand nand_15 (nand_15_out, nand_14_out, nand_9_out);
  nand nand_16 (nand_16_out, nand_11_out, clock_1_out, nand_17_out);
  nand nand_17 (nand_17_out, nand_16_out, clock_1_out, nand_12_out);
  nand nand_18 (nand_18_out, nand_30_out, nand_13_out);
  nand nand_19 (nand_19_out, nand_13_out, nand_29_out);
  LED led_5 (.in(nand_14_out));
  LED led_6 (.in(nand_15_out));
  nand nand_20 (nand_20_out, nand_16_out, nand_21_out);
  nand nand_21 (nand_21_out, nand_20_out, nand_17_out);
  nand nand_22 (nand_22_out, not_S_6, nand_18_out, nand_23_out);
  nand nand_23 (nand_23_out, nand_22_out, nand_19_out, not_R_5);
  nand nand_24 (nand_24_out, nand_59_out, nand_59_out);
  LED led_7 (.in(nand_20_out));
  LED led_8 (.in(nand_21_out));
  nand nand_25 (nand_25_out, nand_22_out, T_2);
  nand nand_26 (nand_26_out, T_2, nand_23_out);
  nand nand_27 (nand_27_out, \С_2 , \С_2 );
  nand nand_28 (nand_28_out, C_6, C_6);
  nand nand_29 (nand_29_out, not_S_6, nand_25_out, nand_30_out);
  nand nand_30 (nand_30_out, nand_29_out, nand_26_out, not_R_5);
  nand nand_31 (nand_31_out, nand_59_out, nand_27_out);
  nand nand_32 (nand_32_out, nand_27_out, nand_24_out);
  nand nand_33 (nand_33_out, nand_61_out, J, C_5);
  nand nand_34 (nand_34_out, C_5, K, nand_60_out);
  nand nand_35 (nand_35_out, nand_63_out, J_2, nand_28_out);
  nand nand_36 (nand_36_out, nand_28_out, K_2, nand_62_out);
  nand nand_37 (nand_37_out, \С , \С );
  LED led_9 (.in(nand_29_out));
  LED led_10 (.in(nand_30_out));
  nand nand_38 (nand_38_out, not_S_7, nand_31_out, nand_39_out);
  nand nand_39 (nand_39_out, nand_38_out, nand_32_out, not_R_7);
  nand nand_40 (nand_40_out, not_S_8, nand_33_out, nand_41_out);
  nand nand_41 (nand_41_out, nand_40_out, nand_34_out, not_R_8);
  nand nand_42 (nand_42_out, not_S_9, nand_35_out, nand_43_out);
  nand nand_43 (nand_43_out, nand_42_out, nand_36_out, not_R_9);
  nor nor_1 (nor_1_out, R, nor_2_out);
  nor nor_2 (nor_2_out, nor_1_out, S);
  nand nand_44 (nand_44_out, S_3, nand_37_out);
  nand nand_45 (nand_45_out, nand_37_out, R_3);
  nand nand_46 (nand_46_out, D_2, C_3);
  nand nand_47 (nand_47_out, C_3, nand_46_out);
  Clock clock_2 (.out(clock_2_out));
  nand nand_48 (nand_48_out, nand_38_out, \С_2 );
  nand nand_49 (nand_49_out, \С_2 , nand_39_out);
  nand nand_50 (nand_50_out, nand_40_out, nand_33_out, nand_34_out);
  nand nand_51 (nand_51_out, nand_34_out, nand_33_out, nand_41_out);
  nand nand_52 (nand_52_out, nand_42_out, C_6);
  nand nand_53 (nand_53_out, C_6, nand_43_out);
  LED led_11 (.in(nor_1_out));
  LED led_12 (.in(nor_2_out));
  nand nand_54 (nand_54_out, not_S_2, nand_44_out, nand_55_out);
  nand nand_55 (nand_55_out, nand_54_out, nand_45_out, not_R_2);
  LED led_13 (.in(nand_56_out));
  nand nand_56 (nand_56_out, nand_46_out, nand_57_out);
  nand nand_57 (nand_57_out, nand_56_out, nand_47_out);
  LED led_14 (.in(nand_57_out));
  nor nor_3 (nor_3_out, nor_5_out, not_S_4);
  nor nor_4 (nor_4_out, not_R_4, nor_6_out);
  Clock clock_3 (.out(clock_3_out));
  nand nand_58 (nand_58_out, not_S_7, nand_48_out, nand_59_out);
  nand nand_59 (nand_59_out, nand_58_out, nand_49_out, not_R_7);
  nand nand_60 (nand_60_out, not_S_8, nand_61_out, nand_50_out);
  nand nand_61 (nand_61_out, nand_51_out, nand_60_out, not_R_8);
  nand nand_62 (nand_62_out, not_S_9, nand_52_out, nand_63_out);
  nand nand_63 (nand_63_out, nand_62_out, nand_53_out, not_R_9);
  nand nand_64 (nand_64_out, nand_54_out, \С );
  nand nand_65 (nand_65_out, \С , nand_55_out);
  nor nor_5 (nor_5_out, nor_3_out, clock_2_out, nor_6_out);
  nor nor_6 (nor_6_out, nor_5_out, clock_2_out, nor_4_out);
  nand nand_66 (nand_66_out, nand_70_out, nand_72_out);
  nand nand_67 (nand_67_out, nand_73_out, nand_71_out);
  LED led_15 (.in(nand_58_out));
  LED led_16 (.in(nand_59_out));
  LED led_17 (.in(nand_60_out));
  LED led_18 (.in(nand_61_out));
  LED led_19 (.in(nand_62_out));
  LED led_20 (.in(nand_63_out));
  nand nand_68 (nand_68_out, not_S_2, nand_64_out, nand_69_out);
  nand nand_69 (nand_69_out, nand_68_out, nand_65_out, not_R_2);
  nor nor_7 (nor_7_out, nor_5_out, nor_8_out);
  nor nor_8 (nor_8_out, nor_7_out, nor_6_out);
  nand nand_70 (nand_70_out, nand_66_out, clock_3_out, nand_71_out);
  nand nand_71 (nand_71_out, nand_70_out, clock_3_out, nand_67_out);
  LED led_21 (.in(nand_68_out));
  LED led_22 (.in(nand_69_out));
  LED led_23 (.in(nor_7_out));
  LED led_24 (.in(nor_8_out));
  nand nand_72 (nand_72_out, nand_70_out, not_S_5, nand_73_out);
  nand nand_73 (nand_73_out, nand_72_out, not_R_6, nand_71_out);
  LED led_25 (.in(nand_72_out));
  LED led_26 (.in(nand_73_out));

  // Notes on the sheet:
  //   C
  //   Q
  //   Q
  //   not Q
  //   not Q
  //   Q
  //   not Q
  //   Q
  //   not Q
  //   Q
  //   not Q
  //   C
  //   Q
  //   not Q
  //   T
  //   Q
  //   not Q
  //   Q
  //   not Q
  //   Q
  //   not Q
  //   Q
  //   not Q
  //   Q
  //   not Q
  //   Q
  //   not Q
  //   Q
  //   not Q
endmodule
