// Logisim project grDeltaMem.circ as structural Verilog: 1 circuit, main circuit grnDeltaMem
module grnDeltaMem (
  input  [6:0] in_1,
  output [23:0] out_2
);

  ROM #(.addrWidth(7), .dataWidth(24)) rom_1 (.addr(in_1), .data(out_2));  // open: sel

  // Notes on the sheet:
  //   contents of rom_1 (hex, n*v repeats v):
  //   1e 1e023 41022 63021 84023 a701e c5025 ea023 10d023 130001 13101e 14f01e 16d01e 18b01e 1a901e 1c701e
  //   1e501e 20301f 22201e 24001e 25e01e 27c01e 29a01f 2b9020 2d901f 2f801f 31701f 33601f 35501f 37401e
  //   39201e 3b0020 3d001e 3ee01f 40d01f 42c01f 44b020 46b01f 48a01f 4a901f 4c801f 4e701f 50601f 52501f
  //   54401f 56301f 58201f 5a101f 5c001e 5de01e 5fc01d 61901c 63501c 65101c 66d01d 68a01c 6a601d 6c301d
  //   6e001e 6fe01c 71a011 72b01c 747890
endmodule
