// Logisim project grnMem2.circ as structural Verilog: 1 circuit, main circuit grnMem2
module grnMem2 (
  input  [6:0] in_1,
  output [31:0] out_2
);

  ROM #(.addrWidth(7), .dataWidth(32)) rom_1 (.addr(in_1), .data(out_2));  // open: sel

  // Notes on the sheet:
  //   contents of rom_1 (hex, n*v repeats v):
  //   204e821 204e822 204e823 204e824 204e825 204e826 204e827 204e828 204e829 204e863 a04e821 a04e822
  //   a04e823 a04e824 a04e825 a04e826 a04e827 a04e828 a04e829 a04e860 a04e861 a04e862 a04e863 a04e864
  //   a04e865 a04e866 a04e867 a04e868 a04e869 a04e8a0 a04e8a1 a04e8a2 a04e8a3 a04e8a4 a04e8a5 a04e8a6
  //   a04e8a7 a04e8a8 a04e8a9 a04e8e0 a04e8e1 a04e8e2 a04e8e3 a04e8e4 a04e8e5 a04e8e6 a04e8e7 a04e8e8
  //   c04e821 c04e822 d04e821 d04e822 d04e823 d04e824 d04e825 d04e826 d04e827 d04e828 d04e829 d04e860
  //   d04e861 d04e862 700f011
endmodule
