// Logisim project stnMem1.circ as structural Verilog: 1 circuit, main circuit stnMem1
module stnMem1 (
  input  [11:0] in_1,
  output [31:0] out_2
);

  ROM #(.addrWidth(12), .dataWidth(32)) rom_1 (.addr(in_1), .data(out_2));  // open: sel

  // Notes on the sheet:
  //   contents of rom_1 (hex, n*v repeats v):
  //   b2cb0041 b2cb2cb2 b2cb2cb0 b2cb2cb2 b2cb2cb0 b2cb2cb0 b2cb2cb0 b2cb2c1c b2cb2cb2 b2cb2cb2 b2cb2c28
  //   b2cb0a40 b2cb2cb0 b2cb0c00 b2cb2c30 b2cb2cb2 b2c3c008 b2c3c549 b2cb2cb0 b2cb2cb1 b2cb104d b2cb2cb1
  //   b2cb1120 b2cb2c45 b2cb2cb2 b2cb2cb2 b2cb2cb2 b2cb2c5c b2cb2cb2 b2cb2cb2 b2cb2cb0 b2cb2cb2 b2cb2c04
  //   b0200b20 b2c0ce40 b2cb2cb0 b2cb2c10 b2cb0714 b2cb2c28 b2cb2cb2 b2cb2c28 b2cb2cb0 b2cb2cb0 b2cb2c2c
  //   b2cb2cb2 b2cb2cb0 b2cb2cb0 b2cb2c30 b2c30840 b2cb2cb2 b2cb2c34 b2cb2cb2 b2cb2cb2 b2cb2cb2 b2c40045
  //   b2cb2cb2 b2cb2cb2 b2cb2cb1 b2cb2c44 b2cb2cb1 b2cb2cb1 b2cb2cb1 b2cb2c5c b2cb2c5c b2cb2cb1 b002c529
  //   b2cb0041 b2cb2cb2 b2cb2cb0 b2cb2cb2 b2cb2c08 b2cb2cb2 b2cb2cb0 b2cb2cb0 b2cb2cb2 b2cb2cb0 b2cb2cb0
  //   b2cb2c28 b2c28e18 b2cb2cb2 b2cb0b21 b2cb2c30 b2cb0c00 b2cb0c00 b2cb2c30 b2cb2c34 b2cb2cb0 b2c3ce2c
  //   b2cb1001 b2cb2c40 b2cb2cb2 b2cb2cb1 b2cb2cb1 b2cb2c49 b2cb2c49 b2cb2cb1 5d33d020 b2cb2c60 b2cb1f29
  //   b2c01400 b2cb2cb2 b2cb2cb2 b2cb2cb2 b2cb0140 b2cb014d b2cb2c08 b2cb2c0c b2cb2c0d b2cb2cb0 b2cb2c10
  //   b2cb2c10 b2cb2cb0 b2cb2cb2 b2cb2cb0 b2cb2cb0 b2cb2c28 b2cb2c28 b2cb2c29 b2cb2cb2 b2cb2cb2 b2c3825c
  //   b2c3c041 b2cb2c3c b2cb0f38 b0f38d38 b2cb2cb2 b2c44f21 b2cb2cb1 b2cb2cb2 b2cb2cb1 b2c5401c b2cb2cb1
  //   93002c b2cb2cb2 b2cb2cb0 b2cb2cb2 b2cb2c05 b2cb2c08 b0301100 b2cb2cb0 b2cb2cb0 b2cb0700 b2cb0a21
  //   b2cb2cb2 b2cb2cb0 b2cb2c28 b2cb2c28 b2cb2cb2 b2c3002c b2cb2c30 b2cb2c30 b2cb2c38 b2cb2c3c b2cb2c3c
  //   b2cb2cb2 b2cb2cb2 b2cb2cb2 b2cb2c50 b2c5082c b2cb1501 b2cb2cb1 b2cb2cb2 b2cb2cb2 b2cb2c60 b2cb2cb2
  //   b2cb2cb2 b2cb2cb1 b0024401 b2cb2c00 b2cb2cb0 b2cb2cb0 b2cb2cb2 b2cb2cb2 b2cb2cb2 b2c28e34 b2c28e34
  //   b2cb2cb2 b2cb2c34 b2cb0f38 b2cb2c40 b2cb2cb1 b2cb2c40 b2cb2c41 b2cb2c44 b2cb2cb2 b2cb2c44 b2cb2c44
  //   b2cb2cb1 b2cb2cb2 b2cb2cb1 b2c5082c b2cb2cb2 b2cb2cb2 b2cb1701 b2cb2cb1 b2cb2cb2 b2cb2cb2 b2cb2cb2
  //   b2cb2cb0 b2c04041 b2cb2c08 b2cb0220 b2cb2cb2 b2cb2cb0 b0714778 b2cb2c1c 2800414d b2cb2c28 b2cb2c29
  //   b2cb2cb2 b2cb2cb0 b2cb2cb0 b2cb2c2c b2cb2cb0 b2cb2cb0 b2cb2cb2 b2cb2cb2 b2cb2cb2 b2cb2c31 b2cb2c3c
  //   b2cb0f2c b2cb2cb0 b2cb2c3c b0f40e54 b2cb2cb2 b2cb2c41 b2cb2cb1 b1138a38 b2cb2cb2 b2cb2cb2 b2cb2cb2
  //   b2cb2cb1 b2cb2cb2 b2cb2cb2 b002c529 b2cb2c00 b2cb2cb2 b2cb2cb2 b2cb2cb0 b2cb2cb2 b2cb2c04 b2cb0338
  //   b2cb2cb2 b2cb2c11 b2c1c530 b2cb2cb0 b2cb2c28 b2cb2c28 b2cb2c30 b2cb2cb0 b2cb2c34 b2cb2c34 b0e0ce40
  //   b2cb2cb2 b2cb2cb0 b2cb0f5c b2cb107c b2cb2c44 b2cb2cb1 b2cb1201 b2cb2c48 b2cb2cb2 b2cb1501 b2cb2cb2
  //   b2cb2c5c b2cb2cb2 b2cb002c b2cb2cb2 b2cb2cb2 b2cb21b0 b2cb22b0 b2cb23b0 b2cb24b0 b2cb25b0 b2cb26b0
  //   b2cb27b0 b2cb28b0 b2cb29b0 b2c860b0 b2c861b0 b2c862b0 b2c863b0 b2c864b0 b2c865b0 b2c866b0 b2c867b0
  //   b2c868b0 b2c869b0 b2c8a0b0 b2c8a1b0 b2c8a2b0 b2c8a3b0 b2c8a4b0 b2c8a5b0 b2c8a6b0 b2c8a7b0 b2c8a8b0
  //   b2c8a9b0 b2c8e0b0 b2c8e1b0 b2c8e2b0 b2c8e3b0 b2c8e4b0 b2c8e5b0 b2cb2c00 b2c00b7d b2cb0041 b2cb2c04
  //   b2c0452c b2cb2cb0 b2cb2cb0 b2cb2c08 b2cb2cb0 b2cb2cb0 b2cb2cb2 b2cb2cb2 b2cb2cb2 b2cb2cb0 b2c29020
  //   b2cb2cb2 b2cb2cb0 b2c30025 b2cb2c38 b2cb2cb2 b2c3c041 b2cb2cb2 b2cb2cb1 b2cb2cb1 b2cb2cb2 b2cb2cb1
  //   b2cb1714 b2cb2cb1 b2cb2cb2 b2cb2cb1 b2cb2c00 b2cb2cb0 b2cb2cb0 b2cb2cb2 b2cb2cb0 b2c0ce40 b2cb2cb2
  //   b2cb2cb2 b2c1c008 b2cb0700 b2cb2cb0 b2c2803c b2cb2c28 b2cb2cb2 b2c2c508 b2cb2cb0 b2cb2cb0 b2cb2cb2
  //   b2cb2cb2 b2cb2cb2 b2c39149 b2cb2cb2 b2c3c549 b2cb0f38 b2cb2cb1 b2cb107c b2cb2cb1 b2cb2cb1 b2cb2cb2
  //   b2cb2cb2 b2cb2cb2 b2cb2cb0 b2cb2cb2 b2cb2cb0 b2cb2cb0 b2cb2cb0 ce2ce10 b2cb2cb0 b2cb2c0d b2cb2c20
  //   b2cb2c28 b2cb2c28 b2cb2cb0 b2cb2cb2 b2cb2cb0 4*b2cb2cb2 b2cb2c3c b2cb0f38 b2cb2cb0 b2cb2cb1 b2cb2cb1
  //   b2cb2c48 b2cb2cb2 b2cb2c5c b2cb2cb1 b2cb2cb1 b2cb2cb1 30030011 b2cb2cb0 b2cb2c04 b2c0402c b2cb2cb0
  //   b2c08860 b2cb2c0c 4*b2cb2cb0 b2cb2cb2 b2cb2cb0 b2cb2cb0 b2cb2c2c b2c2d329 b2cb2cb0 b2cb2cb0 b2cb0c14
  //   b2c31340 b2cb0d14 b2cb2cb2 b2cb2cb0 b2cb0f40 b2cb2cb1 b2cb2c45 b2cb2cb2 b2cb2cb1 b2cb2cb1 b2cb2cb2
  //   b2cb2c3c b2cb0004 111328 b2cb2cb0 b2cb002c 400c04d b2cb2cb0 b2cb2cb0 b2cb2cb0 b2cb064d b2cb2cb0
  //   1c530b14 b2cb2cb2 b2cb2c28 b2cb2cb0 b2cb2cb0 b2cb2c2d b2cb2cb2 b2cb2cb0 b2cb2cb0 b2cb2cb2 b2cb2cb2
  //   b2cb2cb2 b2cb2cb1 b2cb2cb1 b2cb2cb2 b2cb2c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
endmodule
