// Logisim project stnMem2.circ as structural Verilog: 1 circuit, main circuit stnMem2
module stnMem2 (
  input  [11:0] in_1,
  output [31:0] out_2
);

  ROM #(.addrWidth(12), .dataWidth(32)) rom_1 (.addr(in_1), .data(out_2));  // open: sel

  // Notes on the sheet:
  //   contents of rom_1 (hex, n*v repeats v):
  //   200c38d3 c0503847 14cb00d3 cb016ca3 32c010a3 32d360a3 70034cb2 531128e0 cb082dc2 cb0a14b2 e2c844d6
  //   9714d2 a4cb1083 a01014d2 2db5483 cb0c0153 b38244a0 21714d2 f38b1594 14470a2 530034e0 12043903
  //   d70478a3 238b7d03 c45b4883 c51038b3 c5880883 804828e0 cb174c92 c6050452 3444051 cb004127 4526d01
  //   54c1523 e05714d2 33903953 509f48a2 b38244a2 4000801 c2881c83 e3c524a2 a39038b1 a3971523 4a3822
  //   c2c044a3 b38100d3 c00b6c32 540534a3 e35714d2 c3134001 828e2c01 c3c008b3 c3d714b2 c3db60a2 23900d31
  //   c4051cd2 c40e18a3 100c0500 e2ce09c1 348534a3 41443903 438c14d2 540d14d2 544d38a3 f28e08b1 100d1103
  //   114d49c1 cb007813 10014d02 cb2cb020 4482dc1 c10e2c33 438b20d2 46c33847 cb0714d2 778300d3 80cd0123
  //   4120023 508d20a3 c29078a3 27cd44a2 29120c3 d00534a3 d4d70107 51021441 828e2c01 f15240e0 828034e0
  //   144a0073 e10838d3 c40e18a3 6c10171 238a0101 38858a0 33434d13 500c2123 aa8c00b2 52ca3822 33485c50
  //   d0117050 cb010012 cb011504 c04b20d3 51c64cd3 3405850 41200d3 e4010127 2033907 34cc1503 e4041881
  //   e40e10d3 76d07cd3 c20200d3 a2c560d2 a3816d23 e40e48a3 e44d20a3 31107d81 c2db4801 c3453163 834d20a3
  //   538c14d2 e2c54801 b7cd44a2 c01014d2 c4402cc2 20438d3 14c104e4 c45344b3 40041450 80802c81 84c200b3
  //   548420d3 cb002c81 2dc08e4 cb0114b3 34005ca3 e40e05c1 d04528e0 52c84451 70082883 b20200a2 24cd2171
  //   c28e1c51 a3876d01 e2cc6ca3 e2ce3444 cb0b1523 60a1422 51021441 849714d2 a39038a3 60a4d03 e2d20021
  //   cb0f6c63 c48a0174 c4907ca2 82c83cf3 83cf3822 70124d03 54c40123 c5c84801 cb180103 55400963 cb0b0013
  //   cb0d0d31 320c2 b2050 a14d49c1 22072122 70023847 cb080401 cb082dc2 c28e1cb3 440049c1 e34548e0
  //   c2ce04e1 50ce08e4 b7cd44a2 11714d2 77cf3 e3003574 331f3561 4040107 cb110174 840e48a2 e2ce09c1
  //   14d500d3 cb120100 21501553 830e34e0 c50e4851 c55000c3 138244a2 800c20b3 cb2c6021 c60860a2 cb002c51
  //   4124ca3 b60d20a3 4482dc1 a48e40e0 c08e2ca3 551014c3 b20d44a2 834e09c1 8b150181 e2c80401 329360a2
  //   cb0a4cb2 a4cb70a3 a4d00113 508858a2 b14c1582 b20f0123 c30040a2 c3083401 cb0c38a2 340060e0 4056083
  //   e48d20a3 f3833917 e48530a2 e41714d2 cb0f4c77 f04834a3 100b70a2 b38244a2 c4521567 c4d10171 cb1820b3
  //   84c200b3 cb184d23 cb1f0961 100d1103 d21120c3 c0120022 cb010032 100b00a2 cb010117 52df34a3 b38200d3
  //   c10e2801 4c620d2 b7cd20a2 a20d2194 840814d2 e45c7cd3 28b0182 c14138d2 50cc0123 54521503 e10d20a3
  //   c39120f3 f15020c1 52c83561 700d5850 e2ce09c1 14804161 a00d3 830e3483 cb2cb122 220534a3 c5c040a2
  //   84527ca3 cb2c7911 c01001f4 c5405081 cb153803 35*20102003 210514d2 348420d3 200c38d3 2c03442 e28b38a3
  //   139014d2 200300d3 4482dc1 301120b2 32102171 cb073903 c20200d3 c21100a3 a00700a3 23914c43 c29330f0
  //   b2041881 149014d2 a4cd70a3 c3c034e0 538c14d2 c3c54903 14c2073 114d70a2 cb160101 608548a3 13920101
  //   720a4cd3 cb182014 f28e08b1 140000c7 14df60a2 20034cb2 c08e2ca3 239038d2 e60d20a3 c10e0814 c10e2c33
  //   2dc44a2 271f2ce0 70150103 848e34e0 400a910 cb0b0102 400d44a0 c0022c01 c2174d02 c3401131 cb0d20b3
  //   c38d2194 38244a2 c3c060a2 1728e0 b7cd44a2 4c414d2 45c828e0 114c14d3 41443903 cb171522 cb1720a3
  //   cb184d06 4b0050 c0452df1 120a3001 14d26d01 200b70a3 14244a0 340804a3 e4041887 334049c1 2c83483
  //   e40e48a3 a4cb20a3 c2937cd3 c00c1443 cb0c4d52 cb0d3913 c3901553 c3c060a3 549354e0 428e2c72 f38b7ca3
  //   38c0183 12c81ca3 a01714d2 cb2c4d13 84527ca3 80102013 82804133 f44034a2 1520c1 45200d2 5b3483 d340e0
  //   14cb7161 d14244a2 9020b3 34cb7ca2 400d20b3 414d2113 440e1c43 c20200d3 a39038b1 a4133cd3 e0c220d3
  //   c7cd14d2 c00c2123 c0127952 b70d20a3 8858a2 c3892883 cb0f38f3 f3904450 e3c04522 7cf38b3 240560d1
  //   c4904d13 345220d3 44081102 cb2c7d82 844048a3 40534e0 40830e0 2440103 529114d2 210834e0 23903811
  //   33903953 601020a3 22c50 70124cb2 414b7161 c2804050 40f0171 a08044d3 b2150171 f0ce58a2 cb0b7d53
  //   c0112ce0 c2151450 c38b7cd2 cb103830 cb106c10 6c100a3 114c14d3 cb112073 138a38b3 e2ce3051 d38244a0
  //   c5c02907 525714d2 8400b7 c04e28e1 e40e05c1 34e08e0 34c700d3 c1433903 34d20a3 2cc6ca3 b20a4d82
  //   e2c844d6 35220d3 cb0a3913 a4130cb3 c2c04522 b20c38d3 c7cd14d2 c0093903 82940187 d0072103 c38b14d1
  //   b38244a0 cb0f38f3 20d58c0 3953903 3ce3ce4 10046ca3 101020a3 14d3482 c6003401 e3c02ce0 c0405414
  //   54056402 22c044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
endmodule
